// Digital circuit gaming alu.dig as structural Verilog
module gaming_alu (
  input  [7:0] A,
  input  [7:0] B,
  input  [3:0] S,
  input  M,
  input  Cin,
  output [7:0] Out,
  output Cout,
  output A_eq_B
);

  wire _74181_1_pin7, A_B, and_1_out, Arith, Cin_t, driver_10_out, not_2_out, Shift_Left, Shift_RIght, Sign,
       undriven, undriven_2, undriven_3;
  wire [0:0] rom_1_d;
  wire [7:0] _74181_2_pin9, multiplexer_1_out, multiplexer_2_out;
  wire [7:7] multiplexer_3_out, multiplexer_4_out;

  not not_1 (Cin_t, Cin);
  _74181 _74181_1 (
    .pin1(B[4]), .pin2(A[4]), .pin3(S[3]), .pin4(S[2]), .pin5(S[1]), .pin6(S[0]), .pin7(_74181_1_pin7),
    .pin8(M), .pin9(_74181_2_pin9[4]), .pin10(_74181_2_pin9[5]), .pin11(_74181_2_pin9[6]), .pin12(1'b0));  // open: pin13, pin14, pin15, pin16, pin17, pin18, pin19, pin20, pin21, pin22, pin23, pin24
  _74181 _74181_2 (
    .pin1(B[0]), .pin2(A[0]), .pin3(S[3]), .pin4(S[2]), .pin5(S[1]), .pin6(S[0]), .pin7(Cin), .pin8(M),
    .pin9(_74181_2_pin9[0]), .pin10(_74181_2_pin9[1]), .pin11(_74181_2_pin9[2]), .pin12(1'b0));  // open: pin13, pin14, pin15, pin16, pin17, pin18, pin19, pin20, pin21, pin22, pin23, pin24
  Multiplexer #(.Bits(8)) multiplexer_1 (.sel(A_B), .in_0(A), .in_1(B), .out(multiplexer_1_out));
  Multiplexer #(.Bits(8)) multiplexer_2 (.sel(A_B), .in_0(A), .in_1(B), .out(multiplexer_2_out));
  and and_1 (and_1_out, undriven, undriven_2);
  ROM #(.AddrBits(5), .Bits(6)) rom_1 (
    .A({M, S}), .sel(1'b1), .D({A_B, Arith, Shift_RIght, Shift_Left, Sign, rom_1_d[0]}));
  Multiplexer multiplexer_3 (.sel(A_B), .in_0(A[7]), .in_1(B[7]), .out(multiplexer_3_out[7]));
  Multiplexer multiplexer_4 (.sel(Arith), .in_0(Cin_t), .in_1(multiplexer_2_out[7]), .out(multiplexer_4_out[7]));
  assign A_eq_B = rom_1_d[0] ? and_1_out : 1'bz;  // Driver driver_1
  assign Out = rom_1_d[0] ? _74181_2_pin9 : 8'bz;  // Driver driver_2
  assign A_eq_B = Sign ? 1'b0 : 1'bz;  // Driver driver_3
  assign Out = Sign ? {8{multiplexer_3_out[7]}} : 8'bz;  // Driver driver_4
  assign A_eq_B = Shift_Left ? 1'b0 : 1'bz;  // Driver driver_5
  assign Out = Shift_Left ? {multiplexer_1_out[6:0], Cin_t} : 8'bz;  // Driver driver_6
  assign A_eq_B = Shift_RIght ? 1'b0 : 1'bz;  // Driver driver_7
  assign Out = Shift_RIght ? {multiplexer_4_out[7], multiplexer_2_out[7:1]} : 8'bz;  // Driver driver_8
  assign Cout = rom_1_d[0] ? undriven_3 : 1'bz;  // Driver driver_9
  assign Cout = ~rom_1_d[0] ? not_2_out : 1'bz;  // DriverInvSel driverinvsel_1
  not not_2 (not_2_out, driver_10_out);
  assign driver_10_out = Sign ? 1'b0 : 1'bz;  // Driver driver_10
  assign driver_10_out = Shift_Left ? multiplexer_1_out[7] : 1'bz;  // Driver driver_11
  assign driver_10_out = Shift_RIght ? multiplexer_2_out[0] : 1'bz;  // Driver driver_12

  // Notes on the sheet:
  //   contents of rom_1 (hex, n*v repeats v):
  //   20,4,5,20,6,7,20,8,9,20,10,11,20,20,20,20,20,20,20,20,20,20,20,20,20,20,20,20,20,
  //   20,20,20
endmodule
