// Digital circuit gaming cache.dig as structural Verilog
module gaming_cache (
  input  [15:0] A,
  input  str,
  input  ld,
  input  C,
  input  mready,
  output [7:0] Dbus,
  output [7:0] Dram,
  output sr,
  output lr,
  output [15:0] Aram,
  output ready
);

  wire block_index_ovf, undriven;
  wire [13:6] tag_q;

  // And and_1 has open pins: In_1=A[9], In_2=A[10], In_3=A[11], In_4=A[12], In_5=A[13], In_6=A[14], In_7=A[15], out=open
  Counter #(.Bits(2)) block_index (.C(undriven), .out(Aram[1:0]), .ovf(block_index_ovf));  // open: en, clr
  Register #(.Bits(14)) tag (.C(undriven), .Q({tag_q, Aram[7:2]}));  // open: D, en
  Register #(.Bits(7)) tag_valid ();  // open: D, C, en, Q
  Register #(.Bits(15)) tag_valid_2 ();  // open: D, C, en, Q
  RAMDualPort #(.AddrBits(3), .Bits(8)) block ();  // open: A, Din, str, C, ld, D
  RAMDualPort #(.Bits(8)) block_2 ();  // open: A, Din, str, C, ld, D
  // Pins of 8 and 16 bits meet at Aram

  // Other names for the same wires on the sheet: Clock = C

  // Notes on the sheet:
  //   A: Address
  //   str: Store
  //   ld: Load
  //   Dbus: Bidirectional data
  //   Main Cache
  //   128 bytes, 4 byte blocks
  //   2-way set associative
  //   Stack Cache
  //   (upper 512)
  //   32 bytes, 8 byte blocks
  //   Direct mapped
  //   Stack Block
  //   Main Block
  //   RAM Driver
endmodule
