// Digital circuit gaming pc.dig as structural Verilog
module gaming_pc (
  input  clk
);

  wire Address_High_Read, Address_Low_Read, ALU_Enable, and_1_out, and_2_out, and_3_out, and_4_out,
       and_5_out, BP_Direction, BP_Enable, BP_Write, Carry, Carry_Flag_q, Carry_Write, CF_Invert, Cin_Select,
       Comparator_Select, Condition_Enable, Condition_Flag_q, Condition_Invert, Condition_Out,
       Condition_Write, d_ff_1_nq, gaming_alu_1_a_eq_b, gaming_alu_1_cout, IO_Read, IO_Write, IP_Conditional,
       IP_Enable, IP_Write, M, Memory_Load, Memory_Store, multiplexer_2_out, multiplexer_3_out,
       Next_Instruction, not_1_out, or_1_out, or_2_out, Reg_A_Read, Reg_A_Write, Reg_B_Read, Reg_B_Write, S0,
       S1, S2, S3, SP_Direction, SP_Enable, SP_Write, xor_1_out, xor_2_out;
  wire [1:0] Address_Select;
  wire [2:0] Bus_Select;
  wire [4:0] Stage_Counter_out;
  wire [6:0] driver_1_out;
  wire [7:0] A, B, gaming_alu_1_out, Instruction_q, keyboard_1_d;
  wire [7:7] driver_1_out_2;
  wire [15:0] BP, IP_out, multiplexer_1_out, Stack_Pointer_out;
  wire [15:8] keyboard_1_d_2;
  wire [31:0] counter_1_out;

  D_FF d_ff_1 (.D(1'b1), .C(clk), .nQ(d_ff_1_nq));  // open: Q
  or or_1 (or_1_out, IP_Write, Condition_Out);
  or or_2 (or_2_out, d_ff_1_nq, SP_Enable);
  Register #(.Bits(8)) Register_A (.D({driver_1_out_2[7], driver_1_out}), .C(clk), .en(Reg_A_Write), .Q(A));
  Register #(.Bits(8)) Register_B (.D({driver_1_out_2[7], driver_1_out}), .C(clk), .en(Reg_B_Write), .Q(B));
  CounterPreset #(.Bits(16)) Base_Pointer (
    .en(BP_Enable), .C(clk), .dir(BP_Direction), .in(multiplexer_1_out), .ld(BP_Write), .clr(1'b0), .out(BP));  // open: ovf
  CounterPreset #(.Bits(16)) Stack_Pointer (
    .en(or_2_out), .C(clk), .dir(~SP_Direction), .in(multiplexer_1_out), .ld(SP_Write), .clr(1'b0),
    .out(Stack_Pointer_out));  // open: ovf
  CounterPreset #(.Bits(16)) IP (
    .en(IP_Enable), .C(clk), .dir(1'b0), .in(multiplexer_1_out), .ld(or_1_out), .clr(1'b0), .out(IP_out));  // open: ovf
  Register #(.Bits(8)) Instruction (
    .D({driver_1_out_2[7], driver_1_out}), .C(clk), .en(Next_Instruction), .Q(Instruction_q));
  Counter #(.Bits(5)) Stage_Counter (.en(1'b1), .C(clk), .clr(Next_Instruction), .out(Stage_Counter_out));  // open: ovf
  Counter #(.Bits(32)) counter_1 (.en(1'b1), .C(clk), .clr(1'b0), .out(counter_1_out));  // open: ovf
  // Probe SP on Stack_Pointer_out
  // Probe IP on IP_out
  // Probe Instruction on Instruction_q
  // Probe Stage on Stage_Counter_out
  // Probe Total Cycles on counter_1_out
  assign {driver_1_out_2[7], driver_1_out} = Reg_B_Read ? B : 8'bz;  // Driver driver_1
  Multiplexer #(.Selector_Bits(2), .Bits(16)) multiplexer_1 (
    .sel(Address_Select), .in_0({A, B}), .in_1(BP), .in_2(Stack_Pointer_out), .in_3(IP_out),
    .out(multiplexer_1_out));
  ROM #(.AddrBits(13), .Bits(32)) Control_ROM (
    .A({Instruction_q, Stage_Counter_out}), .sel(1'b1),
    .D({IO_Write, Condition_Enable, Condition_Write, Condition_Invert, Comparator_Select, Carry_Write, Cin_Select, CF_Invert, Carry, M, S3, S2, S1, S0, Next_Instruction, IP_Enable, IP_Write, IP_Conditional, SP_Enable, SP_Direction, SP_Write, BP_Enable, BP_Direction, BP_Write, Reg_B_Write, Reg_A_Write, Memory_Store, Bus_Select, Address_Select}));
  assign {driver_1_out_2[7], driver_1_out} = Address_Low_Read ? multiplexer_1_out[7:0] : 8'bz;  // Driver driver_2
  assign {driver_1_out_2[7], driver_1_out} = Address_High_Read ? multiplexer_1_out[15:8] : 8'bz;  // Driver driver_3
  // Probe Address on multiplexer_1_out
  // Probe BP on BP
  and and_1 (and_1_out, multiplexer_1_out[15], Memory_Store);
  and and_2 (and_2_out, multiplexer_1_out[15], Memory_Load);
  not not_1 (not_1_out, multiplexer_1_out[15]);
  and and_3 (and_3_out, not_1_out, Memory_Load);
  // Probe Bus on {driver_1_out_2[7], driver_1_out}
  assign {driver_1_out_2[7], driver_1_out} = Reg_A_Read ? A : 8'bz;  // Driver driver_4
  // Probe A on A
  // Probe B on B
  RAMSinglePort #(.AddrBits(15), .Bits(8)) _32kx8_RAM (
    .A(multiplexer_1_out[14:0]), .str(and_1_out), .C(clk), .ld(and_2_out),
    .D({driver_1_out_2[7], driver_1_out}));
  ROM #(.AddrBits(15), .isProgramMemory("true"), .Bits(8)) _32kx8_ROM (
    .A(multiplexer_1_out[14:0]), .sel(and_3_out), .D({driver_1_out_2[7], driver_1_out}));
  Demultiplexer #(.Selector_Bits(3)) demultiplexer_1 (
    .sel(Bus_Select), .in(1'b1), .out_0(Memory_Load), .out_1(ALU_Enable), .out_2(Reg_A_Read),
    .out_3(Reg_B_Read), .out_4(Address_Low_Read), .out_5(Address_High_Read), .out_6(IO_Read));  // open: out_7
  Terminal terminal_1 (.D(driver_1_out), .C(clk), .en(IO_Write));
  assign {driver_1_out_2[7], driver_1_out} = IO_Read ? keyboard_1_d : 8'bz;  // Driver driver_5
  Keyboard keyboard_1 (.C(clk), .en(IO_Read), .D({keyboard_1_d_2, keyboard_1_d}));  // open: av
  and and_4 (and_4_out, clk, Carry_Write);
  Multiplexer multiplexer_2 (.sel(Cin_Select), .in_0(Carry_Flag_q), .in_1(Carry), .out(multiplexer_2_out));
  D_FF Carry_Flag (.D(xor_1_out), .C(and_4_out), .Q(Carry_Flag_q));  // open: nQ
  gaming_alu gaming_alu_1 (
    .A(A), .B(B), .S({S3, S2, S1, S0}), .M(M), .Cin(multiplexer_2_out), .Out(gaming_alu_1_out),
    .Cout(gaming_alu_1_cout), .A_eq_B(gaming_alu_1_a_eq_b));
  xor xor_1 (xor_1_out, gaming_alu_1_cout, CF_Invert);
  Multiplexer multiplexer_3 (
    .sel(Comparator_Select), .in_0(gaming_alu_1_cout), .in_1(gaming_alu_1_a_eq_b), .out(multiplexer_3_out));
  assign {driver_1_out_2[7], driver_1_out} = ALU_Enable ? gaming_alu_1_out : 8'bz;  // Driver driver_6
  and and_5 (and_5_out, clk, Condition_Write);
  D_FF Condition_Flag (.D(multiplexer_3_out), .C(and_5_out), .Q(Condition_Flag_q));  // open: nQ
  xor xor_2 (xor_2_out, Condition_Flag_q, Condition_Invert);
  and and_6 (Condition_Out, xor_2_out, Condition_Enable);

  // Other names for the same wires on the sheet: Clock = clk

  // Notes on the sheet:
  //   clk: Hz: 10
  //   contents of Control_ROM (hex, n*v repeats v):
  //   30023,0,0,0,0,0,0,0,0,0,0,0,0,0,0,0,0,0,0,0,0,0,0,0,0,0,0,0,0,0,0,0,12123,b2,30023,
  //   0,0,0,0,0,0,0,0,0,0,0,0,0,0,0,0,0,0,0,0,0,0,0,0,0,0,0,0,0,12123,10223,20b6,b2,30023,
  //   0,0,0,0,0,0,0,0,0,0,0,0,0,0,0,0,0,0,0,0,0,0,0,0,0,0,0,33023,0,0,0,0,0,0,0,0,0,0,0,
  //   0,0,0,0,0,0,0,0,0,0,0,0,0,0,0,0,0,0,0,0,3000,33023,0,0,0,0,0,0,0,0,0,0,0,0,0,0,0,
  //   0,0,0,0,0,0,0,0,0,0,0,0,0,0,0,12a,10223,6a40224,16a,124,2820,30023,0,0,0,0,0,0,0,
  //   0,0,0,0,0,0,0,0,0,0,0,0,0,0,0,0,0,0,2122,b2,30023,0,0,0,0,0,0,0,0,0,0,0,0,0,0,0,0,
  //   0,0,0,0,0,0,0,0,0,0,0,0,0,0,0,0,0,0,0,0,0,0,0,0,0,0,0,0,0,0,0,0,0,0,0,0,0,0,0,0,0,
  //   0,0,0,0,0,0,0,0,0,0,0,0,0,0,0,0,0,0,0,0,0,0,0,0,0,0,0,0,0,0,0,0,0,0,0,0,0,0,0,0,0,
  //   0,0,0,0,0,0,0,0,0,0,0,0,0,0,0,0,0,0,0,0,0,0,0,0,0,0,0,3122,2222,2000,20b6,b2,30023,
  //   0,0,0,0,0,0,0,0,0,0,0,0,0,0,0,0,0,0,0,0,0,0,0,0,0,0,0,0,0,0,0,0,0,0,0,0,0,0,0,0,0,
  //   0,0,0,0,0,0,0,0,0,0,0,0,0,0,0,0,0,0,0,0,0,0,0,0,0,0,0,0,0,0,0,0,0,0,0,0,0,0,0,0,0,
  //   0,0,0,0,0,0,0,0,0,0,0,0,0,0,0,0,0,0,0,0,0,0,0,0,0,0,0,0,0,0,0,0,0,0,0,0,0,0,0,0,0,
  //   0,0,0,0,0,0,0,0,0,0,0,0,0,0,0,0,0,0,0,0,0,0,0,0,0,0,0,0,0,0,0,0,0,0,0,0,0,0,0,0,0,
  //   0,0,0,0,0,0,0,0,0,0,0,0,0,0,0,0,0,0,0,0,0,0,3122,222,20b2,b6,30023,0,0,0,0,0,0,0,
  //   0,0,0,0,0,0,0,0,0,0,0,0,0,0,0,0,0,0,0,0,3122,3000,222,20b2,2122,30b6,3000,3000,222,
  //   20b2,2000,20b6,30023,0,0,0,0,0,0,0,0,0,0,0,0,0,0,0,0,0,0,0,0,0,0,0,0,0,0,0,0,0,0,
  //   0,0,0,0,0,0,0,0,0,0,0,0,0,0,0,0,0,0,0,0,0,0,0,0,0,0,0,0,0,0,0,0,0,0,0,0,0,0,0,0,0,
  //   0,0,0,0,0,0,0,0,0,0,0,0,0,0,0,0,0,0,0,0,0,0,0,0,0,0,0,0,0,0,0,0,0,0,0,0,0,0,0,0,0,
  //   0,0,0,0,0,0,0,0,0,0,0,0,0,0,0,0,0,0,0,0,0,0,0,0,0,0,0,0,0,0,0,0,0,0,0,0,0,0,0,0,0,
  //   0,0,0,0,0,0,0,0,0,0,0,0,0,0,0,0,0,0,0,0,0,0,0,0,0,0,0,0,0,0,0,0,0,0,0,0,0,0,0,0,0,
  //   0,0,0,0,0,0,0,0,0,0,0,0,0,0,0,0,0,0,0,0,0,0,0,0,0,0,0,0,0,0,0,0,0,0,0,0,0,0,0,0,0,
  //   0,0,0,0,0,0,0,0,0,0,0,0,0,0,0,0,0,0,0,0,0,0,0,0,0,0,0,0,0,0,0,0,0,0,0,0,0,0,0,0,0,
  //   0,0,0,0,0,0,0,0,0,0,0,0,0,0,0,0,0,0,0,0,0,0,0,0,0,0,0,0,0,0,0,0,0,0,0,0,0,0,0,0,0,
  //   0,0,0,0,0,0,0,0,0,0,0,0,0,0,0,0,0,0,0,0,0,0,0,0,0,0,0,0,0,0,0,0,0,0,0,0,0,0,0,0,0,
  //   0,0,0,0,0,0,0,0,0,0,0,0,0,0,0,0,0,0,0,0,0,0,0,0,0,0,0,0,0,0,0,0,0,0,0,0,0,0,0,0,0,
  //   0,0,0,0,0,0,0,0,0,0,0,0,0,0,0,0,0,0,0,0,0,0,0,0,0,0,0,0,0,0,0,0,0,0,0,0,0,0,0,0,0,
  //   0,0,0,0,0,0,0,0,0,0,0,0,0,0,0,0,0,0,0,0,0,0,0,0,0,0,0,10223,10123,2120,b2,30023,0,
  //   0,0,0,0,0,0,0,0,0,0,0,0,0,0,0,0,0,0,0,0,0,0,0,0,0,0,3222,122,120,b2,30023,0,0,0,0,
  //   0,0,0,0,0,0,0,0,0,0,0,0,0,0,0,0,0,0,0,0,0,0,0,3122,7b00222,c20a6,6a430a6,3222,2122,
  //   242124,3222,3120,b2,30023,0,0,0,0,0,0,0,0,0,0,0,0,0,0,0,0,0,0,0,0,0,2122,7b10223,
  //   c30a6,6a420a6,3222,10123,240124,222,120,b2,30023,0,0,0,0,0,0,0,0,0,0,0,0,0,0,0,0,
  //   0,0,0,0,0,0,0,0,0,0,0,0,0,0,0,0,0,0,0,0,0,0,0,0,0,0,0,0,0,0,0,0,0,0,0,0,0,0,0,0,0,
  //   0,0,0,0,0,0,0,0,0,0,0,0,0,0,0,0,0,0,0,0,0,0,0,0,0,0,0,0,0,0,0,0,0,0,0,0,0,0,0,0,0,
  //   0,0,0,0,0,0,0,0,0,0,0,0,0,0,0,0,0,0,0,0,0,0,0,0,0,0,0,0,0,0,0,0,0,0,0,0,0,0,0,0,0,
  //   0,0,0,0,0,0,0,0,0,0,10223,10123,400,122,30b1,30023,0,0,0,0,0,0,0,0,0,0,0,0,0,0,0,
  //   0,0,0,0,0,0,0,0,0,0,0,2169,b2,2129,b2,13223,13123,400,2122,20b1,3222,3122,3400,30023,
  //   0,0,0,0,0,0,0,0,0,0,0,0,0,0,0,0,0,0,0,0,0,0,0,0,0,0,0,0,0,0,0,0,0,0,0,0,0,0,0,0,0,
  //   0,0,0,0,0,0,0,0,0,0,0,0,0,0,0,0,0,0,0,0,0,0,0,0,0,0,0,0,0,0,0,0,0,0,0,0,0,0,0,0,0,
  //   0,0,0,0,0,0,0,0,0,0,0,0,0,0,0,0,0,0,0,0,0,0,0,0,0,0,0,0,0,0,0,0,0,0,0,0,0,0,0,0,0,
  //   0,0,0,0,0,0,0,0,0,0,0,0,0,0,0,0,0,0,0,0,0,0,0,0,0,0,0,0,0,0,0,0,0,0,0,0,0,0,0,0,0,
  //   0,0,0,0,0,0,0,0,0,0,0,0,0,0,0,0,0,0,0,0,0,0,0,0,0,0,0,0,0,0,0,0,0,0,0,0,0,0,0,0,0,
  //   0,0,0,0,0,0,0,0,0,0,0,0,0,0,0,0,0,0,0,0,0,0,0,0,0,0,0,0,0,0,0,0,0,0,0,0,0,0,0,0,0,
  //   0,0,0,0,0,0,0,0,0,0,0,0,0,0,0,0,0,0,0,0,0,0,0,0,0,0,0,0,0,0,0,0,0,0,0,0,0,0,0,0,0,
  //   0,0,0,0,0,0,0,0,0,0,0,0,0,0,0,0,0,0,0,0,0,0,0,0,0,0,0,0,0,0,0,0,0,0,0,0,0,0,0,0,0,
  //   0,0,0,0,0,0,0,0,0,0,0,0,0,0,0,0,0,0,0,0,0,0,0,0,0,0,0,0,0,0,0,0,0,0,0,0,0,0,0,0,0,
  //   0,0,0,0,0,0,0,0,0,0,0,0,0,0,0,0,0,0,0,0,0,0,0,0,0,0,0,0,0,0,0,0,0,0,0,0,0,0,0,0,0,
  //   0,0,0,0,0,0,0,0,0,0,0,0,0,0,0,0,0,0,0,0,0,0,0,0,0,0,0,0,0,0,0,0,0,0,0,0,0,0,0,0,0,
  //   0,0,0,0,0,0,0,0,0,0,0,0,0,0,0,0,0,0,0,0,0,0,0,0,0,0,0,0,0,0,0,0,0,0,0,0,0,0,0,0,0,
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  //   contents of _32kx8_ROM (hex, n*v repeats v):
  //   1,20,1,69,1,68,ff,ff,ff,81,f6,0,2000,300,6300,2300,ff00,100,ff000,2300,0,100,ff00,
  //   2300,0,1000,ff00,100,e900,8000,0,0,0,0,0,0,0,0,0,0,0,0,0,0,0,0,0,0,0,0,0,0,0,0,0,
  //   0,0,0,0,0,0,0,0,0,0,0,0,0,0,0,0,0,0,0,0,0,0,0,0,0,0,0,0,0,0,0,0,0,0,0,0,0,0,0,0,0,
  //   0,0,0,0,0,0,0,0,0,0,0,0,0,0,0,0,0,0,0,0,0,0,0,0,0,0,0,0,0,0,0,0,0,0,0,0,0,0,0,0,0,
  //   0,0,0,0,0,0,0,0,0,0,0,0,0,0,0,0,0,0,0,0,0,0,0,0,0,0,0,0,0,0,0,0,0,0,0,0,0,0,0,0,0,
  //   0,0,0,0,0,0,0,0,0,0,0,0,0,0,0,0,0,0,0,0,0,0,0,0,0,0,0,0,0,0,0,0,0,0,0,0,0,0,0,0,0,
  //   0,0,0,0,0,0,0,0,0,0,0,7a,79,78,77,76,75,74,73,72,71,70,6f,6e,6d,6c,6b,6a,69,68,67,
  //   66,65,64,63,62,61,20,61,62,63,64,65,66,67,68,69,6a,6b,6c,6d,6e,6f,70,71,72,43,74,
  //   75,76,77,78,79,7a
endmodule
